// Digital circuit part_c.dig as structural Verilog
module part_c (
  input  in_0,
  input  in_1,
  input  in_2,
  output out_0
);

  wire fgpfet_1_d, fgpfet_2_d, fgpfet_3_d, fgpfet_5_d, fgpfet_8_d, fgpfet_9_d, fgpfet_10_d, fgpfet_11_d,
       nfet_3_s, nfet_5_s, nfet_6_s;

  FGPFET fgpfet_1 (.G(in_0), .S(1'b1), .D(fgpfet_1_d));
  NFET nfet_1 (.G(in_0), .D(fgpfet_1_d), .S(1'b0));
  FGPFET fgpfet_2 (.G(in_1), .S(1'b1), .D(fgpfet_2_d));
  NFET nfet_2 (.G(in_1), .D(fgpfet_2_d), .S(1'b0));
  FGPFET fgpfet_3 (.G(fgpfet_1_d), .S(1'b1), .D(fgpfet_3_d));
  FGPFET fgpfet_4 (.G(fgpfet_2_d), .S(1'b1), .D(fgpfet_3_d));
  FGPFET fgpfet_5 (.G(in_0), .S(1'b1), .D(fgpfet_5_d));
  FGPFET fgpfet_6 (.G(in_1), .S(1'b1), .D(fgpfet_5_d));
  NFET nfet_3 (.G(fgpfet_1_d), .D(fgpfet_3_d), .S(nfet_3_s));
  NFET nfet_4 (.G(fgpfet_2_d), .D(nfet_3_s), .S(1'b0));
  FGPFET fgpfet_7 (.G(in_2), .S(1'b1), .D(fgpfet_5_d));
  NFET nfet_5 (.G(in_0), .D(fgpfet_5_d), .S(nfet_5_s));
  NFET nfet_6 (.G(in_1), .D(nfet_5_s), .S(nfet_6_s));
  NFET nfet_7 (.G(in_2), .D(nfet_6_s), .S(1'b0));
  FGPFET fgpfet_8 (.G(fgpfet_3_d), .S(1'b1), .D(fgpfet_8_d));
  NFET nfet_8 (.G(fgpfet_3_d), .D(fgpfet_8_d), .S(1'b0));
  FGPFET fgpfet_9 (.G(fgpfet_5_d), .S(1'b1), .D(fgpfet_9_d));
  NFET nfet_9 (.G(fgpfet_5_d), .D(fgpfet_9_d), .S(1'b0));
  FGPFET fgpfet_10 (.G(fgpfet_8_d), .S(1'b1), .D(fgpfet_10_d));
  FGPFET fgpfet_11 (.G(fgpfet_9_d), .S(fgpfet_10_d), .D(fgpfet_11_d));
  NFET nfet_10 (.G(fgpfet_8_d), .D(fgpfet_11_d), .S(1'b0));
  NFET nfet_11 (.G(fgpfet_9_d), .D(fgpfet_11_d), .S(1'b0));
  FGPFET fgpfet_12 (.G(fgpfet_11_d), .S(1'b1), .D(out_0));
  NFET nfet_12 (.G(fgpfet_11_d), .D(out_0), .S(1'b0));
endmodule

/* Test case part_c_test:
in_0 in_1 in_2 out_0
 0    0    0    1
 0    0    1    1
 0    1    0    0
 0    1    1    0
 1    0    0    0
 1    0    1    0
 1    1    0    0
 1    1    1    1
*/
