// Digital circuit lab2_part1.dig as structural Verilog
module lab2_part1 (
  input  inA_0,
  input  inA_1,
  input  inA_2,
  input  inA_3,
  input  inB_0,
  input  inB_1,
  input  inB_2,
  input  inB_3,
  output out0,
  output out1,
  output out2,
  output out3,
  output out_13,
  output out_14
);

  wire aout1, aout2, aout3, aout4, bout1, bout2, bout3, bout4, cout1, cout2, cout3, cout4, dout1, dout2,
       dout3, dout4;

  Demultiplexer #(.Selector_Bits(2)) demultiplexer_1 (
    .sel({inB_1, inB_0}), .in(inA_0), .out_0(aout1), .out_1(aout2), .out_2(aout3), .out_3(aout4));
  Demultiplexer #(.Selector_Bits(2)) demultiplexer_2 (
    .sel({inB_1, inB_0}), .in(inA_1), .out_0(bout1), .out_1(bout2), .out_2(bout3), .out_3(bout4));
  Demultiplexer #(.Selector_Bits(2)) demultiplexer_3 (
    .sel({inB_1, inB_0}), .in(inA_2), .out_0(cout1), .out_1(cout2), .out_2(cout3), .out_3(cout4));
  Demultiplexer #(.Selector_Bits(2)) demultiplexer_4 (
    .sel({inB_1, inB_0}), .in(inA_3), .out_0(dout1), .out_1(dout2), .out_2(dout3), .out_3(dout4));
  or or_1 (out0, aout1, bout4, cout3, dout2);
  or or_2 (out1, aout2, bout1, cout4, dout3);
  or or_3 (out2, aout3, bout2, cout1, dout4);
  or or_4 (out3, aout4, bout3, cout2, dout1);

  assign out_13 = inB_2;
  assign out_14 = inB_3;

  // Notes on the sheet:
  //   Interface (do not edit the content inside this box)
  //   Inputs
  //   Outputs
  //   Rotatee:
  //   Rotation amount:
  //   Result of Rotating  input A by the amount given by input B:
endmodule

/* Test case:
inA_3 inA_2 inA_1 inA_0 inB_1 inB_0  out3 out2 out1 out0
 0     0     0     0     0     0      0    0    0    0  
 0     0     0     1     0     0      0    0    0    1  
 0     0     0     1     0     1      0    0    1    0  
 0     0     0     1     1     0      0    1    0    0  
 0     0     0     1     1     1      1    0    0    0   
 0     1     0     1     0     0      0    1    0    1  
 0     1     0     1     0     1      1    0    1    0  
 0     1     0     1     1     0      0    1    0    1  
 0     1     0     1     1     1      1    0    1    0   
*/
