// Digital circuit lab2_part2.dig as structural Verilog
module lab2_part2 (
  input  in0,
  input  in1,
  input  in2,
  input  in3,
  input  in_21,
  input  in_22,
  input  in_23,
  input  in_24,
  input  in_25,
  input  in_26,
  input  in_27,
  input  in_28,
  output seg_a,
  output seg_f,
  output seg_b,
  output seg_g,
  output seg_e,
  output seg_c,
  output seg_d,
  output seg_dp,
  output sign_a,
  output sign_f,
  output sign_b,
  output sign_g,
  output sign_e,
  output sign_c,
  output sign_d,
  output sign_dp
);

  wire _0, _1, _2, _3, _4, _5, _6, _7, _8, or_2_out, or_4_out, or_6_out, or_8_out, or_12_out, plexout2,
       plexout3, plexout4, plexout5, plexout6, plexout7, plexout8, plexout10, plexout11, plexout12,
       plexout13, plexout14, plexout15, plexout16;

  or or_1 (seg_a, _2, _0, or_2_out, _3, _7);
  or or_2 (or_2_out, _5, _8, _6);
  or or_3 (seg_b, _2, _0, or_4_out, _1, _3);
  or or_4 (or_4_out, _4, _8, _7);
  or or_5 (seg_c, _3, _0, or_6_out, _1, _5);
  or or_6 (or_6_out, _7, _6, _4, _8);
  or or_7 (seg_d, _2, _0, or_8_out, _3, _5);
  or or_8 (or_8_out, _6, _8);
  Demultiplexer #(.Selector_Bits(4)) demultiplexer_1 (
    .sel({in3, in2, in1, in0}), .in(1'b1), .out_0(_0), .out_1(plexout2), .out_2(plexout3), .out_3(plexout4),
    .out_4(plexout5), .out_5(plexout6), .out_6(plexout7), .out_7(plexout8), .out_8(_8), .out_9(plexout10),
    .out_10(plexout11), .out_11(plexout12), .out_12(plexout13), .out_13(plexout14), .out_14(plexout15),
    .out_15(plexout16));
  or or_9 (seg_e, _0, _2, _6, _8);
  or or_10 (seg_f, _5, _0, _8, _6, _4);
  or or_11 (seg_g, _3, _2, or_12_out, _4, _5);
  or or_12 (or_12_out, _6, _8);
  or or_13 (_1, plexout2, plexout16);
  or or_14 (_2, plexout3, plexout15);
  or or_15 (_3, plexout4, plexout14);
  or or_16 (_4, plexout5, plexout13);
  or or_17 (_5, plexout6, plexout12);
  or or_18 (_6, plexout7, plexout11);
  or or_19 (_7, plexout8, plexout10);
  Seven_Seg seven_seg_1 (.a(in_22), .b(in_21), .c(in_26), .d(in_25), .e(in_24), .f(in_23), .g(in3), .dp(in_27));
  Seven_Seg seven_seg_2 (.a(seg_a), .b(seg_b), .c(seg_c), .d(seg_d), .e(seg_e), .f(seg_f), .g(seg_g), .dp(in_28));

  assign seg_dp = in_28;
  assign sign_a = in_22;
  assign sign_b = in_21;
  assign sign_c = in_26;
  assign sign_d = in_25;
  assign sign_dp = in_27;
  assign sign_e = in_24;
  assign sign_f = in_23;
  assign sign_g = in3;

  // Other names for the same wires on the sheet: _1b = _1; _1c = _1; _2a = _2; _2b = _2; _2d = _2; _2e = _2; _2g = _2;
  //   _3a = _3; _3b = _3; _3c = _3; _3d = _3; _3g = _3; _4b = _4; _4c = _4; _4f = _4; _4g = _4; _5a = _5; _5c = _5;
  //   _5d = _5; _5f = _5; _5g = _5; _6a = _6; _6c = _6; _6d = _6; _6e = _6; _6f = _6; _6g = _6; _7a = _7; _7b = _7;
  //   _7c = _7; _0a = _0; _0b = _0; _0c = _0; _0d = _0; _0e = _0; _0f = _0; plexout1 = _0; _8a = _8; _8b = _8;
  //   _8c = _8; _8d = _8; _8e = _8; _8f = _8; _8g = _8; plexout9 = _8

  // Notes on the sheet:
  //   Interface (do not edit the content inside this box)
  //   Outputs:
  //   Inputs
  //   Sign
  //   Decimal Number
endmodule

/* Test case:
in3 in2 in1 in0  sign_a sign_b sign_c sign_d sign_e sign_f sign_g  seg_a seg_b seg_c seg_d seg_e seg_f seg_g
 0   0   0   0    0      0      0      0      0      0      0       1     1     1     1     1     1     0
*/
